// Logisim project halfcyclecounter.circ as structural Verilog: 1 circuit, main circuit main
module main (
  input  in_1,
  input  in_2,
  input  in_3,
  input  in_4,
  input  in_5,
  input  in_6
);

  wire and_1_out, and_2_out, and_3_out, and_4_out, and_5_out, and_6_out, and_7_out, and_8_out, and_9_out,
       and_10_out, and_11_out, and_12_out, and_13_out, and_14_out, and_15_out, clock_1_out, clock_2_out,
       not_1_out, not_2_out, not_3_out, not_4_out, not_5_out, or_1_out, t_ff_1_qn, t_ff_2_qn, t_ff_3_qn,
       t_ff_4_qn;
  wire [2:0] t_ff_1_q, t_ff_2_q;
  wire [3:0] j_k_ff_1_q, j_k_ff_2_q;

  not not_1 (not_1_out, in_2);
  Clock clock_1 (.out(clock_1_out));
  not not_2 (not_2_out, in_5);
  Clock clock_2 (.out(clock_2_out));
  and and_1 (and_1_out, not_1_out, clock_1_out);
  and and_2 (and_2_out, not_2_out, clock_2_out);
  T_Flip_Flop t_ff_1 (.T(in_1), .clk(and_1_out), .Q(t_ff_1_q[0]), .Qn(t_ff_1_qn));  // open: reset, preset
  J_K_Flip_Flop j_k_ff_1 (.J(and_9_out), .K(and_9_out), .clk(and_1_out), .Q(j_k_ff_1_q[0]));  // open: Qn, preset, reset
  T_Flip_Flop t_ff_2 (.T(in_4), .clk(and_2_out), .Q(t_ff_2_q[0]), .Qn(t_ff_2_qn));  // open: reset, preset
  J_K_Flip_Flop j_k_ff_2 (
    .J(and_10_out), .K(and_10_out), .clk(and_2_out), .Q(j_k_ff_2_q[0]));  // open: Qn, preset, reset
  and and_3 (and_3_out, j_k_ff_1_q[0], and_9_out);
  T_Flip_Flop t_ff_3 (.T(t_ff_1_qn), .clk(and_1_out), .Q(t_ff_1_q[1]), .Qn(t_ff_3_qn));  // open: reset, preset
  J_K_Flip_Flop j_k_ff_3 (.J(and_3_out), .K(and_3_out), .clk(and_1_out), .Q(j_k_ff_1_q[1]));  // open: Qn, preset, reset
  T_Flip_Flop t_ff_4 (.T(t_ff_2_qn), .clk(and_2_out), .Q(t_ff_2_q[1]), .Qn(t_ff_4_qn));  // open: reset, preset
  J_K_Flip_Flop j_k_ff_4 (.J(and_4_out), .K(and_4_out), .clk(and_2_out), .Q(j_k_ff_2_q[1]));  // open: Qn, preset, reset
  and and_4 (and_4_out, j_k_ff_2_q[0], and_10_out);
  and and_5 (and_5_out, t_ff_3_qn, t_ff_1_qn);
  T_Flip_Flop t_ff_5 (.T(and_5_out), .clk(and_1_out), .Q(t_ff_1_q[2]));  // open: Qn, reset, preset
  J_K_Flip_Flop j_k_ff_5 (.J(and_6_out), .K(and_6_out), .clk(and_1_out), .Q(j_k_ff_1_q[2]));  // open: Qn, preset, reset
  and and_6 (and_6_out, j_k_ff_1_q[1], and_3_out);
  and and_7 (and_7_out, t_ff_4_qn, t_ff_2_qn);
  and and_8 (and_8_out, j_k_ff_2_q[1], and_4_out);
  and and_9 (and_9_out, or_1_out, in_1);
  T_Flip_Flop t_ff_6 (.T(and_7_out), .clk(and_2_out), .Q(t_ff_2_q[2]));  // open: Qn, reset, preset
  and and_10 (and_10_out, and_15_out, in_4);
  J_K_Flip_Flop j_k_ff_6 (.J(and_8_out), .K(and_8_out), .clk(and_2_out), .Q(j_k_ff_2_q[2]));  // open: Qn, preset, reset
  and and_11 (and_11_out, j_k_ff_1_q[2], and_6_out);
  Hex_Digit_Display hex_digit_display_1 (.value({in_3, t_ff_1_q}));  // open: dp
  not not_3 (not_3_out, t_ff_1_q[0]);
  not not_4 (not_4_out, t_ff_1_q[1]);
  J_K_Flip_Flop j_k_ff_7 (
    .J(and_11_out), .K(and_11_out), .clk(and_1_out), .Q(j_k_ff_1_q[3]));  // open: Qn, preset, reset
  not not_5 (not_5_out, t_ff_2_q[1]);
  and and_12 (and_12_out, j_k_ff_2_q[2], and_8_out);
  and and_13 (and_13_out, not_3_out, not_4_out, t_ff_1_q[2]);
  and and_14 (and_14_out, t_ff_1_q[0], t_ff_1_q[1], t_ff_1_q[2]);
  Hex_Digit_Display hex_digit_display_2 (.value({in_6, t_ff_2_q}));  // open: dp
  and and_15 (and_15_out, t_ff_2_q[0], not_5_out, t_ff_2_q[2]);
  J_K_Flip_Flop j_k_ff_8 (
    .J(and_12_out), .K(and_12_out), .clk(and_2_out), .Q(j_k_ff_2_q[3]));  // open: Qn, preset, reset
  or or_1 (or_1_out, and_13_out, and_14_out);
  Hex_Digit_Display hex_digit_display_3 (.value(j_k_ff_1_q));  // open: dp
  Hex_Digit_Display hex_digit_display_4 (.value(j_k_ff_2_q));  // open: dp
endmodule
